# Fritzing sketch pico-sms-mqtt-gw (saved by Fritzing 1.0.1rc)
breadboards: 2

parts:
  R5 = Resistor [resistance=220 tolerance=±5% power=0.25W package=THT]
  Grove1 = Grove OLED 128x96
  Mod1 = Raspberry Pi Pico W
  SIM800L_BO1 = SIM800L BO
  M1 = RioRand LM2596
  LED1 = smd LED [color="Red (633nm)" package="0805 [SMD]"]
  U1 = SWITCH_SPDT [package=kps-1290]

nets:
  N1: R5.Pin_0, LED1.cathode
  GND: R5.Pin_1, Grove1.GND, Grove1.SCL, Mod1.pin_18, Mod1.pin_28, Mod1.pin_38, Mod1.pin_42, SIM800L_BO1.GND, M1.Pin_2, U1.P
  N2: Grove1.VCC, Mod1.pin_36
  N3: Grove1.SDA, Mod1.pin_19
  N4: Mod1.pin_21, SIM800L_BO1.RXD
  N5: Mod1.pin_22, SIM800L_BO1.TXD
  N6: Mod1.pin_26, LED1.anode
  N7: Mod1.pin_27, U1.S
  N8: Mod1.pin_31, SIM800L_BO1.RST
  N9: Mod1.pin_40, M1.Pin_1
  N10: SIM800L_BO1.VCC, M1.Pin_3

custom parts:
  Raspberry Pi Pico W: Raspberry Pi Pico W. Based around the RP2040 microcontroller the Pico W is a low cost microcontroller device bringing Raspberry Pi quality, cost, and easy of use to the microcontroller space. The areas marked KEEPOUT in pcb silkscreen should not have traces running through them to avoid shorts on a soldered in module!
